# Fritzing sketch pewpew-m4-v8 (saved by Fritzing 0.9.4)
circuit board: 5.21002cm x 8.50001cm
breadboards: 1

parts:
  X1 = USB Connectors [package=usb-microb]
  BAT/USB = SWITCH_SPDT [package=kps-1290]
  - = female pin header, 1 pin [form="♀ (female)"]
  + = female pin header, 1 pin [form="♀ (female)"]
  C2 = Ceramic Capacitor [capacitance=100nF package="0603 [SMD, multilayer]"]
  C1 = Ceramic Capacitor [capacitance=100nF package="0603 [SMD, multilayer]"]
  U2 = ST7735 TFT [part_number=ST7735 package=14pin]
  R1 = Resistor [tolerance=±5% resistance=100k package="0603 [SMD]"]
  -_2 = female pin header, 1 pin [form="♀ (female)"]
  +_2 = female pin header, 1 pin [form="♀ (female)"]
  U1 = QFN-48 [chip_label=IC package=QFN]
  R2 = Resistor [tolerance=±5% resistance=220 package="0603 [SMD]"]
  R3 = Resistor [tolerance=±5% resistance=220 package="0603 [SMD]"]
  U3 = Voltage Regulator LDO [package=sot23-5]
  X3 = Buzzer 7.5mm [package=buzzer-hyg7525]
  BU = Pushbutton [package="[SMD]"]
  BD = Pushbutton [package="[SMD]"]
  BL = Pushbutton [package="[SMD]"]
  BR = Pushbutton [package="[SMD]"]
  BX = Pushbutton [package="[SMD]"]
  BO = Pushbutton [package="[SMD]"]
  BZ = Pushbutton [package="[SMD]"]
  J2 = female alternating pin header, 12 pins [form="♀ (female)"]

nets:
  N1: X1.D+, U1.PA25
  N2: X1.D-, U1.PA24
  GND: X1.GND, -.pin1, C2.1, C1.0, U2.NC, U2.GND, U2.LED-, -_2.pin1, U1.GND, U1.thermal, U3.GND, X3.-, BU.Pin_2, BD.Pin_1, BL.Pin_2, BR.Pin_3, BR.Pin_4, BX.Pin_3, BX.Pin_4, BO.Pin_1, BO.Pin_2, BZ.Pin_1, J2.pin10, J2.pin11
  N3: X1.VBUS, U3.IN, U3.EN
  N4: BAT/USB.O, U3.OUT
  N5: BAT/USB.P, C2.0, U2.VCC, U2.IOVCC, R1.Pin_1, U1.PA03, U1.VDDANA, U1.VDDIO, R2.Pin_0, J2.pin1, J2.pin2
  N6: BAT/USB.S, +.pin1, +_2.pin1
  N7: C1.1, U1.VDDCORE
  N8: U2.LED+, R1.Pin_0
  N9: U2.!RESET, U1.PA17
  N10: U2.D/C, U1.PA16
  N11: U2.MOSI, U1.PA15
  N12: U2.SCK, U1.PA13
  N13: U2.CS, U1.PA11
  N14: U1.PA00, J2.pin7
  N15: U1.PA01, J2.pin6
  N16: U1.PA02, R3.Pin_1, J2.pin5
  N17: U1.PA04, J2.pin4
  N18: U1.PA05, J2.pin3
  N19: U1.PA09, BX.Pin_1, BX.Pin_2
  N20: U1.PA10, BO.Pin_3, BO.Pin_4
  N21: U1.PA22, BZ.Pin_3, BZ.Pin_4
  N22: U1.PA23, BU.Pin_3, BU.Pin_4
  N23: U1.PB22, BR.Pin_1, BR.Pin_2
  N24: U1.PB23, BL.Pin_3, BL.Pin_4
  N25: U1.PA27, BD.Pin_3, BD.Pin_4
  N26: U1.NRESET, R2.Pin_1, J2.pin12
  N27: U1.PA30, J2.pin9
  N28: U1.PA31, J2.pin8
  N29: R3.Pin_0, X3.+

notes:
  PewPew M4 v8.0
  + 3V
  - gnd
  R rst
  1 swc pwm
  2 swd pwm
  3 sda miso mosi pwm tx
  4 scl sck pwm rx
  5 adc dac
  6 adc scl sck tx
  7 sda miso mosi rx
  R - - 1 2 3 4 5 6
  Pew
  M4
  X2
  X4
  z x o
  http://pewpew.rtfd.io

custom parts:
  ST7735 TFT: Connector for 14-pin ST7735 TFT display.
  Buzzer 7.5mm: buzzer 7.5mm
  Pushbutton: A generic pushbutton.
